# Fritzing sketch Servo_Tachometer (saved by Fritzing 0.8.7b)
breadboards: 1

parts:
  U1 = NodeMCU V3.0
  YwRobot_Power_Supply1 = YwRobot Breadboard Power Supply [part_number=545043]
  J1 = Basic Servo
  LED1 = LED - 5mm [color="Red (633nm)" package="5 mm [THT]"]
  R1 = Resistor [tolerance=±5% resistance=220 package=THT]
  U2 = Sharp PC817 [part_number=PC817XI package=SMT]
  R3 = Resistor [tolerance=±5% resistance=4.7k package=THT]
  R2 = Resistor [tolerance=±5% resistance=680 package=THT]

nets:
  N1: U1.D1, LED1.cathode
  N2: U1.D3, U2.Pin_4, R3.Pin_1
  GND: U1.GND, YwRobot_Power_Supply1.GND, J1.gnd, R1.Pin_0, U2.Pin_2, U2.Pin_3
  VCC: YwRobot_Power_Supply1.VCC, J1.vcc, R3.Pin_0
  N3: LED1.anode, R1.Pin_1
  N4: U2.Pin_1, R2.Pin_0

notes:
  INPUT 12V (電門)
  INPUT GND (接地)
  輸出 5V
  伺服馬達 MG995
  INPUT 轉速訊號
  12V 轉 5V，YuRobot 545043
  可用其他 Buck 代替
  Servo 指針式轉速表
  https://3wa.tw
  By 羽山秋人
  2020-06-16
  PC817
  光偶合
  NodeMcu V2
  220Ω
  4.7KΩ
  680Ω
  LED 超轉燈

custom parts:
  NodeMCU V3.0: ESP8266 based NodeMCU
  YwRobot Breadboard Power Supply: The YwRobot Breadboard Power Supply (MB-V2) has two power rails; they can be 5V or 3V3. Power to the module can be provided through the female USB socket or through the A10 (female) 2.1mm power jack.
